// Logisim project CPU_VIX9 (2).circ as structural Verilog: 6 circuits, main circuit main
module main (
);

  wire Clk, ExtOp, ImmSel, MemRd, MemWr, RegSrc, RegWrite, WBdata, zf;
  wire [1:0] AluSel, Funct, PC_ctrl, RegDst;
  wire [2:0] imm5, multiplexer_2_out, multiplexer_3_out;
  wire [3:0] AluOp;
  wire [4:0] opcode, PCSignals;
  wire [5:0] imm11;
  wire [15:0] ALUResult, BusA, BusB, BusW, Immout, multiplexer_1_out, multiplexer_4_out, PC, PC1, ram_1_dout,
       shifter_1_out, Target;

  Clock clock_1 (.out(Clk));
  Multiplexer #(.select(2), .width(16)) multiplexer_1 (
    .in0(PC1), .in1(Target), .in2(BusA), .out(multiplexer_1_out), .sel(PC_ctrl));  // open: in3
  Register #(.width(16)) PC_Register (.D(multiplexer_1_out), .clk(Clk), .Q(PC));  // open: en, clr
  ROM #(.addrWidth(16), .dataWidth(16)) Instruction_memory (.addr(PC), .data({opcode, Funct, imm5, imm11}));
  Adder #(.width(16)) adder_1 (.a(16'h1), .b(PC), .out(PC1));  // open: cin, cout
  Multiplexer #(.select(2), .width(3)) multiplexer_2 (
    .in0(imm5), .in1(imm11[2:0]), .in2(3'b111), .in3(3'b001), .out(multiplexer_2_out), .sel(RegDst));
  Multiplexer #(.width(3)) multiplexer_3 (.in0(imm11[2:0]), .in1(imm5), .out(multiplexer_3_out), .sel(RegSrc));
  Control control_1 (
    .OpCode(opcode), .F(Funct), .ExtOp(ExtOp), .ImmSEL(ImmSel), .RegSrc(RegSrc), .RegDst(RegDst),
    .PCSignals(PCSignals), .AluSel(AluSel), .ALUop(AluOp), .MemWr(MemWr), .MemRd(MemRd), .WBdata(WBdata),
    .RegWrite(RegWrite));
  extender extender_1 (
    .imm5({Funct, imm5}), .imm11({Funct, imm5, imm11}), .ImmSel(ImmSel), .ExtOp(ExtOp), .ImmOUT(Immout));
  RegisterFile registerfile_1 (
    .Rs(imm11[5:3]), .Rt(multiplexer_3_out), .RW(multiplexer_2_out), .RegWrite(RegWrite), .BusW(BusW),
    .clk(Clk), .BusA(BusA), .BusB(BusB));
  Shifter #(.width(16)) shifter_1 (.in(Immout), .\dist (4'b0101), .out(shifter_1_out));
  Multiplexer #(.select(2), .width(16)) multiplexer_4 (
    .in0(BusB), .in1(Immout), .in2(PC1), .in3(shifter_1_out), .out(multiplexer_4_out), .sel(AluSel));
  Adder #(.width(16)) adder_2 (.a(PC), .b(Immout), .out(Target));  // open: cin, cout
  PC_controler pc_controler_1 (.PCSignals(PCSignals), .z(zf), .PC_ctrl(PC_ctrl));
  ALU alu_1 (.A(BusA), .B(multiplexer_4_out), .AluOp(AluOp), .ALU_Result_df3b8835(ALUResult), .ZF(zf));
  RAM #(.addrWidth(16), .asyncread("true"), .dataWidth(16)) ram_1 (
    .addr(ALUResult), .we(MemWr), .oe(MemRd), .clk(Clk), .din(BusB), .dout(ram_1_dout));
  Multiplexer #(.width(16)) multiplexer_5 (.in0(ALUResult), .in1(ram_1_dout), .out(BusW), .sel(WBdata));

  // Other names for the same wires on the sheet: Rt[2:0] = imm11[2:0]; Rs[2:0] = imm11[5:3];
  //   imm11[10:6] = {Funct, imm5}; Rd[2:0] = imm5; imm5[4:3] = Funct

  // Notes on the sheet:
  //   contents of Instruction_memory (hex, n*v repeats v):
  //   ff8f 510a 4783 584c 4bd7 ff 311 5e2 7e2 954 b8a d0b e8a 10e5 130e 14ce 179e 0 1960 1b98 1cd0 69f9
  //   68fc 60fb 7089 522d 7908 522d 522d 522d 8015 17*0 522d 0 522d 5141 880c b50 7000 9*0 5042 5043 d3
  //   29a 47c9 7f41 1e38 292
endmodule

module RegisterFile (
  input  [2:0] Rs,
  input  [2:0] Rt,
  input  [2:0] RW,
  input  RegWrite,
  input  [15:0] BusW,
  input  clk,
  output [15:0] BusA,
  output [15:0] BusB
);

  wire and_1_out, and_2_out, and_3_out, and_4_out, and_5_out, and_6_out, and_7_out, decoder_1_out1,
       decoder_1_out2, decoder_1_out3, decoder_1_out4, decoder_1_out5, decoder_1_out6, decoder_1_out7,
       decoder_2_out0, decoder_2_out1, decoder_2_out2, decoder_2_out3, decoder_2_out4, decoder_2_out5,
       decoder_2_out6, decoder_2_out7, decoder_3_out0, decoder_3_out1, decoder_3_out2, decoder_3_out3,
       decoder_3_out4, decoder_3_out5, decoder_3_out6, decoder_3_out7;
  wire [15:0] R1, R2, R3, R4, R5, R6, R7;

  Decoder #(.enable("false"), .select(3)) decoder_1 (
    .out1(decoder_1_out1), .out2(decoder_1_out2), .out3(decoder_1_out3), .out4(decoder_1_out4),
    .out5(decoder_1_out5), .out6(decoder_1_out6), .out7(decoder_1_out7), .sel(RW));  // open: out0
  and and_1 (and_1_out, decoder_1_out1, RegWrite);
  and and_2 (and_2_out, decoder_1_out2, RegWrite);
  and and_3 (and_3_out, decoder_1_out3, RegWrite);
  and and_4 (and_4_out, decoder_1_out4, RegWrite);
  and and_5 (and_5_out, decoder_1_out5, RegWrite);
  and and_6 (and_6_out, decoder_1_out6, RegWrite);
  and and_7 (and_7_out, decoder_1_out7, RegWrite);
  Register #(.width(16)) u_R1 (.D(BusW), .en(and_1_out), .clk(clk), .Q(R1));  // open: clr
  Register #(.width(16)) u_R2 (.D(BusW), .en(and_2_out), .clk(clk), .Q(R2));  // open: clr
  Register #(.width(16)) u_R3 (.D(BusW), .en(and_3_out), .clk(clk), .Q(R3));  // open: clr
  Register #(.width(16)) u_R4 (.D(BusW), .en(and_4_out), .clk(clk), .Q(R4));  // open: clr
  Register #(.width(16)) u_R5 (.D(BusW), .en(and_5_out), .clk(clk), .Q(R5));  // open: clr
  Register #(.width(16)) u_R6 (.D(BusW), .en(and_6_out), .clk(clk), .Q(R6));  // open: clr
  Register #(.width(16)) u_R7 (.D(BusW), .en(and_7_out), .clk(clk), .Q(R7));  // open: clr
  Decoder #(.enable("false"), .select(3)) decoder_2 (
    .out0(decoder_2_out0), .out1(decoder_2_out1), .out2(decoder_2_out2), .out3(decoder_2_out3),
    .out4(decoder_2_out4), .out5(decoder_2_out5), .out6(decoder_2_out6), .out7(decoder_2_out7), .sel(Rs));
  assign BusA = decoder_2_out1 ? R1 : 16'bz;  // Controlled_Buffer controlled_buffer_1
  assign BusA = decoder_2_out2 ? R2 : 16'bz;  // Controlled_Buffer controlled_buffer_2
  assign BusA = decoder_2_out3 ? R3 : 16'bz;  // Controlled_Buffer controlled_buffer_3
  assign BusA = decoder_2_out4 ? R4 : 16'bz;  // Controlled_Buffer controlled_buffer_4
  assign BusA = decoder_2_out5 ? R5 : 16'bz;  // Controlled_Buffer controlled_buffer_5
  assign BusA = decoder_2_out6 ? R6 : 16'bz;  // Controlled_Buffer controlled_buffer_6
  assign BusA = decoder_2_out7 ? R7 : 16'bz;  // Controlled_Buffer controlled_buffer_7
  assign BusA = decoder_2_out0 ? {16{1'b0}} : 16'bz;  // Controlled_Buffer controlled_buffer_8
  Decoder #(.enable("false"), .select(3)) decoder_3 (
    .out0(decoder_3_out0), .out1(decoder_3_out1), .out2(decoder_3_out2), .out3(decoder_3_out3),
    .out4(decoder_3_out4), .out5(decoder_3_out5), .out6(decoder_3_out6), .out7(decoder_3_out7), .sel(Rt));
  assign BusB = decoder_3_out0 ? {16{1'b0}} : 16'bz;  // Controlled_Buffer controlled_buffer_9
  assign BusB = decoder_3_out1 ? R1 : 16'bz;  // Controlled_Buffer controlled_buffer_10
  assign BusB = decoder_3_out2 ? R2 : 16'bz;  // Controlled_Buffer controlled_buffer_11
  assign BusB = decoder_3_out3 ? R3 : 16'bz;  // Controlled_Buffer controlled_buffer_12
  assign BusB = decoder_3_out4 ? R4 : 16'bz;  // Controlled_Buffer controlled_buffer_13
  assign BusB = decoder_3_out5 ? R5 : 16'bz;  // Controlled_Buffer controlled_buffer_14
  assign BusB = decoder_3_out6 ? R6 : 16'bz;  // Controlled_Buffer controlled_buffer_15
  assign BusB = decoder_3_out7 ? R7 : 16'bz;  // Controlled_Buffer controlled_buffer_16
endmodule

module ALU (
  input  [15:0] A,
  input  [15:0] B,
  input  [3:0] AluOp,
  output [15:0] ALU_Result_df3b8835,
  output ZF
);

  wire comparator_1_lt, comparator_2_lt;
  wire [15:0] adder_1_out, and_1_out, bit_extender_1_out, bit_extender_2_out, not_1_out, or_1_out,
       shifter_1_out, shifter_2_out, shifter_3_out, shifter_4_out, subtractor_1_out, xor_1_out;

  Comparator #(.width(16)) comparator_1 (.a(A), .b(B), .lt(comparator_1_lt));  // open: gt, eq
  Comparator #(.mode("unsigned"), .width(16)) comparator_2 (.a(A), .b(B), .lt(comparator_2_lt));  // open: gt, eq
  assign xor_1_out = A ^ B;  // XOR_Gate xor_1, 16 bits wide
  assign or_1_out = A | B;  // OR_Gate or_1, 16 bits wide
  assign and_1_out = A & B;  // AND_Gate and_1, 16 bits wide
  Shifter #(.width(16)) shifter_1 (.in(A), .\dist (B[3:0]), .out(shifter_1_out));
  Shifter #(.shift("lr"), .width(16)) shifter_2 (.in(A), .\dist (B[3:0]), .out(shifter_2_out));
  Shifter #(.shift("ar"), .width(16)) shifter_3 (.in(A), .\dist (B[3:0]), .out(shifter_3_out));
  Shifter #(.shift("rr"), .width(16)) shifter_4 (.in(A), .\dist (B[3:0]), .out(shifter_4_out));
  assign bit_extender_1_out = {{15{1'b0}}, comparator_1_lt};  // Bit_Extender bit_extender_1
  assign bit_extender_2_out = {{15{1'b0}}, comparator_2_lt};  // Bit_Extender bit_extender_2
  assign not_1_out = ~or_1_out;  // NOT_Gate not_1, 16 bits wide
  Adder #(.width(16)) adder_1 (.a(A), .b(B), .out(adder_1_out));  // open: cin, cout
  Subtractor #(.width(16)) subtractor_1 (.a(A), .b(B), .out(subtractor_1_out));  // open: bin, bout
  Multiplexer #(.select(4), .width(16)) multiplexer_1 (
    .in0(adder_1_out), .in1(subtractor_1_out), .in2(bit_extender_1_out), .in3(bit_extender_2_out),
    .in4(xor_1_out), .in5(or_1_out), .in6(and_1_out), .in7(not_1_out), .in8(shifter_1_out),
    .in9(shifter_2_out), .in10(shifter_3_out), .in11(shifter_4_out),
    .in12({B[15:8], A[0], A[1], A[2], A[3], A[4], A[5], A[6], A[7]}),
    .in13({A[8], A[9], A[10], A[11], A[12], A[13], A[14], A[15], B[7:0]}),
    .in14({A[0], A[1], A[2], A[3], A[4], A[5], A[6], A[7], A[8], A[9], A[10], A[11], A[12], A[13], A[14], A[15]}),
    .in15(B), .out(ALU_Result_df3b8835), .sel(AluOp));
  Comparator #(.width(16)) comparator_3 (.a(ALU_Result_df3b8835), .b({16{1'b0}}), .eq(ZF));  // open: gt, lt

  // Other names for the same wires on the sheet: Ra[15:0] = A; Rb[15:0] = B; ShftAmnt[3:0] = B[3:0]

  // Notes on the sheet:
  //   SLL
  //   SRL
  //   SRA
  //   SLT
  //   SLTU
  //   ROR
endmodule

module Control (
  input  [4:0] OpCode,
  input  [1:0] F,
  output ExtOp,
  output ImmSEL,
  output RegSrc,
  output [1:0] RegDst,
  output [4:0] PCSignals,
  output [1:0] AluSel,
  output [3:0] ALUop,
  output MemWr,
  output MemRd,
  output WBdata,
  output RegWrite
);

  wire Addi, Addr, ANDI, ANDr, LUI, NORr, or_1_out, or_2_out, or_4_out, or_5_out, or_6_out, or_7_out,
       or_8_out, or_9_out, or_10_out, or_11_out, ORI, ORr, R0_Type, R1_Type, R2_Type, REVA, REVH, REVL, RORr,
       SLLr, SLTr, SLTUr, SRAr, SRLr, Subr, XORI, XORr;

  Decoder #(.select(5)) decoder_1 (
    .out0(R0_Type), .out1(R1_Type), .out2(R2_Type), .out3(RegSrc), .out8(Addi), .out9(ANDI), .out10(ORI),
    .out11(XORI), .out12(MemRd), .out13(MemWr), .out14(PCSignals[4]), .out15(PCSignals[3]),
    .out16(PCSignals[1]), .out17(PCSignals[2]), .out31(LUI), .sel(OpCode));  // open: out4, out5, out6, out7, out18, out19, out20, out21, out22, out23, out24, out25, out26, out27, out28, out29, out30, en
  Decoder #(.select(2)) decoder_2 (.out0(Addr), .out1(Subr), .out2(SLTr), .out3(SLTUr), .sel(F), .en(R0_Type));
  Decoder #(.select(2)) decoder_3 (.out0(ANDr), .out1(ORr), .out2(XORr), .out3(NORr), .sel(F), .en(R1_Type));
  Decoder #(.select(2)) decoder_4 (.out0(SLLr), .out1(SRLr), .out2(SRAr), .out3(RORr), .sel(F), .en(R2_Type));
  Decoder #(.select(2)) decoder_5 (.out0(REVL), .out1(REVH), .out2(REVA), .out3(PCSignals[0]), .sel(F), .en(RegSrc));
  or or_1 (or_1_out, MemWr, MemRd, Addi, ANDI, ORI, XORI);
  or or_2 (or_2_out, R1_Type, R0_Type, R2_Type, RegSrc, PCSignals[3], PCSignals[4]);
  nor nor_1 (ExtOp, XORI, ORI, ANDI);
  or or_3 (ImmSEL, LUI, PCSignals[1], PCSignals[2]);
  Priority_Encoder #(.select(2)) priority_encoder_1 (
    .in0(or_2_out), .in1(or_1_out), .in2(PCSignals[2]), .in3(LUI), .out(AluSel));  // open: gs, en_out, en_in
  nor nor_2 (RegWrite, PCSignals[3], PCSignals[4], MemWr, PCSignals[1]);
  or or_4 (or_4_out, ANDr, ANDI);
  or or_5 (or_5_out, ORr, ORI);
  or or_6 (or_6_out, XORr, XORI);
  or or_7 (or_7_out, PCSignals[2], LUI);
  or or_8 (or_8_out, PCSignals[4], PCSignals[3], Subr);
  or or_9 (or_9_out, MemWr, MemRd, Addi, ANDI, ORI, XORI);
  or or_10 (or_10_out, Addr, MemRd, MemWr, Addi);
  Priority_Encoder #(.select(4)) priority_encoder_2 (
    .in0(or_10_out), .in1(or_8_out), .in2(SLTr), .in3(SLTUr), .in4(or_6_out), .in5(or_5_out), .in6(or_4_out),
    .in7(NORr), .in8(SLLr), .in9(SRLr), .in10(SRAr), .in11(RORr), .in12(REVL), .in13(REVH), .in14(REVA),
    .in15(or_7_out), .out(ALUop));  // open: gs, en_out, en_in
  or or_11 (or_11_out, R1_Type, R0_Type, R2_Type, RegSrc, PCSignals[3], PCSignals[4]);
  Priority_Encoder #(.select(2)) priority_encoder_3 (
    .in0(or_11_out), .in1(or_9_out), .in2(PCSignals[2]), .in3(LUI), .out(RegDst));  // open: gs, en_out, en_in

  assign WBdata = MemRd;

  // Other names for the same wires on the sheet: LW = MemRd; JR = PCSignals[0]; J = PCSignals[1]; JAL = PCSignals[2];
  //   BNE = PCSignals[3]; BEQ = PCSignals[4]; R3_Type = RegSrc; SW = MemWr
endmodule

module extender (
  input  [4:0] imm5,
  input  [10:0] imm11,
  input  ImmSel,
  input  ExtOp,
  output [15:0] ImmOUT
);

  wire [15:0] bit_extender_1_out, bit_extender_2_out, bit_extender_3_out, bit_extender_4_out,
       multiplexer_1_out, multiplexer_2_out;

  assign bit_extender_1_out = {{11{imm5[4]}}, imm5};  // Bit_Extender bit_extender_1
  assign bit_extender_2_out = {{11{imm5[4]}}, imm5};  // Bit_Extender bit_extender_2
  assign bit_extender_3_out = {{5{imm11[10]}}, imm11};  // Bit_Extender bit_extender_3
  assign bit_extender_4_out = {{5{imm11[10]}}, imm11};  // Bit_Extender bit_extender_4
  Multiplexer #(.width(16)) multiplexer_1 (
    .in0(bit_extender_1_out), .in1(bit_extender_2_out), .out(multiplexer_1_out), .sel(ExtOp));
  Multiplexer #(.width(16)) multiplexer_2 (
    .in0(bit_extender_3_out), .in1(bit_extender_4_out), .out(multiplexer_2_out), .sel(ExtOp));
  Multiplexer #(.width(16)) multiplexer_3 (
    .in0(multiplexer_1_out), .in1(multiplexer_2_out), .out(ImmOUT), .sel(ImmSel));
endmodule

module PC_controler (
  input  [4:0] PCSignals,
  input  z,
  output [1:0] PC_ctrl
);

  wire and_1_out, and_2_out, nor_1_out, not_1_out, or_1_out;

  not not_1 (not_1_out, z);
  and and_1 (and_1_out, PCSignals[3], not_1_out);
  and and_2 (and_2_out, PCSignals[4], z);
  or or_1 (or_1_out, PCSignals[1], PCSignals[2], and_1_out, and_2_out);
  nor nor_1 (nor_1_out, or_1_out, PCSignals[0]);
  Priority_Encoder #(.select(2)) priority_encoder_1 (
    .in0(nor_1_out), .in1(or_1_out), .in2(PCSignals[0]), .out(PC_ctrl));  // open: in3, gs, en_out, en_in

  // Other names for the same wires on the sheet: JR = PCSignals[0]; J = PCSignals[1]; JAL = PCSignals[2];
  //   BNE = PCSignals[3]; BEQ = PCSignals[4]; zf = z
endmodule
